# Fritzing sketch analog (saved by Fritzing 0.9.3b)

parts:
  U1 = NodeMCU v1
  R1 = Photocell (LDR) [package=THT]
  R2 = Resistor [tolerance=±5% resistance=220 package=THT]

nets:
  N1: U1.connector5, R1.pin_1
  N2: U1.connector16, R2.Pin_0
  N3: U1.connector42, R1.pin_0, R2.Pin_1
