# Fritzing sketch blink (saved by Fritzing 0.9.3b)

parts:
  U1 = NodeMCU v1
  LED1 = LED - 5mm [color="Red (633nm)" package="5 mm [THT]"]
  R1 = Resistor [tolerance=±5% resistance=220 package=THT]

nets:
  N1: U1.connector6, LED1.cathode
  N2: U1.connector7, R1.Pin_0
